# Fritzing sketch Connector Breadboard (saved by Fritzing 0.9.0b)

parts:
  proto1 = Adafruit_PermaProto_1_4_Board
  J1 = Screw terminal - 2 pins [package=THT]  # not connected
  J3 = Screw terminal - 2 pins [package=THT]  # not connected
  J4 = Screw terminal - 2 pins [package=THT]  # not connected
  J5 = Screw terminal - 2 pins [package=THT]  # not connected
  J6 = female pin header, 2 pins [form="♀ (female)"]  # not connected
  J7 = female pin header, 2 pins [form="♀ (female)"]  # not connected
  J8 = female pin header, 2 pins [form="♀ (female)"]  # not connected
  J9 = female pin header, 2 pins [form="♀ (female)"]  # not connected
  Part1 = Adafruit LSM9DS1 9DoF Breakout [part_number="Adafruit #3387"]  # not connected
  J10 = female pin header, 2 pins [form="♀ (female)"]  # not connected
  J11 = female pin header, 2 pins [form="♀ (female)"]

nets:
  N1: proto1.connectorB6, J11.pin2

custom parts:
  Adafruit LSM9DS1 9DoF Breakout: Add motion, direction and orientation sensing to your Arduino project with this all-in-one 9-DOF sensor. Inside the chip are three sensors, one is a classic 3-axis accelerometer, which can tell you which direction is down towards the Earth (by measuring gravity) or how fast the board is accelerating in 3D space. The other is a 3-axis magnetometer that can sense where the strongest magnetic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
