# Fritzing sketch PID-Stand-Electronics (saved by Fritzing 0.9.0b)
breadboards: 1

parts:
  proto1 = Adafruit_PermaProto_1_4_Board
  J1 = Screw terminal - 2 pins [package=THT]  # not connected
  J2 = Screw terminal - 2 pins [package=THT]  # not connected
  J3 = Screw terminal - 2 pins [package=THT]  # not connected
  J4 = Screw terminal - 2 pins [package=THT]  # not connected
  Part1 = Adafruit LSM9DS1 9DoF Breakout [part_number="Adafruit #3387"]
  C6 = Electrolytic Capacitor [capacitance=10μF package="0605 [SMD, electrolytic]"]
  C7 = Electrolytic Capacitor [capacitance=10μF package="0605 [SMD, electrolytic]"]
  C8 = Electrolytic Capacitor [capacitance=10μF package="0605 [SMD, electrolytic]"]
  C9 = Electrolytic Capacitor [capacitance=10μF package="0605 [SMD, electrolytic]"]
  D5 = Schottky Diode [part_number=1N5817 package="300 mil [THT]"]
  D6 = Schottky Diode [part_number=1N5817 package="300 mil [THT]"]
  D7 = Schottky Diode [part_number=1N5817 package="300 mil [THT]"]
  D8 = Schottky Diode [part_number=1N5817 package="300 mil [THT]"]
  MOTOR5 = Vibration Motor  # not connected
  FET5 = STP16NF06 N-Channel Power MOSFET
  MOTOR6 = Vibration Motor  # not connected
  MOTOR7 = Vibration Motor  # not connected
  MOTOR8 = Vibration Motor  # not connected
  FET6 = STP16NF06 N-Channel Power MOSFET
  FET7 = STP16NF06 N-Channel Power MOSFET
  FET8 = STP16NF06 N-Channel Power MOSFET
  R5 = Resistor [tolerance=±5% resistance=220 package="1206 [SMD]"]
  R6 = Resistor [tolerance=±5% resistance=220 package="1206 [SMD]"]
  R7 = Resistor [tolerance=±5% resistance=220 package="1206 [SMD]"]
  R8 = Resistor [tolerance=±5% resistance=220 package="1206 [SMD]"]
  Part2 = Arduino Uno (Rev3)

nets:
  N1: proto1.connectorA7, Part2.A4/SDA
  N2: proto1.connectorA8, Part2.A5/SCL
  N3: proto1.connectorC1, D6.anode, FET6.drain
  N4: proto1.connectorC15, D5.anode, FET5.drain
  N5: proto1.connectorH1, D8.anode, FET7.drain
  N6: proto1.connectorH15, D7.anode, FET8.drain
  N7: proto1.connectorW4, Part1.VIN
  N8: proto1.connectorW10, Part2.VIN
  N9: proto1.connectorW13, proto1.connectorY13
  N10: proto1.connectorX6, Part1.GND
  N11: proto1.connectorX10, Part2.GND
  N12: C6.-, FET5.source
  N13: C6.+, D5.cathode
  N14: C7.-, FET6.source
  N15: C7.+, D6.cathode
  N16: C8.-, FET7.source
  N17: C8.+, D8.cathode
  N18: C9.-, FET8.source
  N19: C9.+, D7.cathode
  N20: FET5.gate, R5.Pin_1
  N21: FET6.gate, R6.Pin_1
  N22: FET7.gate, R7.Pin_1
  N23: FET8.gate, R8.Pin_1

custom parts:
  Adafruit LSM9DS1 9DoF Breakout: Add motion, direction and orientation sensing to your Arduino project with this all-in-one 9-DOF sensor. Inside the chip are three sensors, one is a classic 3-axis accelerometer, which can tell you which direction is down towards the Earth (by measuring gravity) or how fast the board is accelerating in 3D space. The other is a 3-axis magnetometer that can sense where the strongest magnetic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
  Vibration Motor: An eccentric vibration motor!
  STP16NF06 N-Channel Power MOSFET: STP16NF06 N-channel Power MOSFET
