# Fritzing sketch Breadboard Version (saved by Fritzing 0.9.0b)
breadboards: 1

parts:
  C1 = Electrolytic Capacitor [capacitance=10μF package="0605 [SMD, electrolytic]"]
  D1 = Schottky Diode [part_number=1N5817 package="300 mil [THT]"]
  FET1 = STP16NF06 N-Channel Power MOSFET
  MOTOR1 = Vibration Motor
  R1 = Resistor [tolerance=±5% resistance=220 package="1206 [SMD]"]
  C3 = Electrolytic Capacitor [capacitance=10μF package="0605 [SMD, electrolytic]"]
  D2 = Schottky Diode [part_number=1N5817 package="300 mil [THT]"]
  FET2 = STP16NF06 N-Channel Power MOSFET
  MOTOR2 = Vibration Motor
  R2 = Resistor [tolerance=±5% resistance=220 package="1206 [SMD]"]
  R3 = Resistor [tolerance=±5% resistance=220 package="1206 [SMD]"]
  D3 = Schottky Diode [part_number=1N5817 package="300 mil [THT]"]
  FET3 = STP16NF06 N-Channel Power MOSFET
  C4 = Electrolytic Capacitor [capacitance=10μF package="0605 [SMD, electrolytic]"]
  C5 = Electrolytic Capacitor [capacitance=10μF package="0605 [SMD, electrolytic]"]
  D4 = Schottky Diode [part_number=1N5817 package="300 mil [THT]"]
  FET4 = STP16NF06 N-Channel Power MOSFET
  R4 = Resistor [tolerance=±5% resistance=220 package="1206 [SMD]"]
  MOTOR3 = Vibration Motor
  MOTOR4 = Vibration Motor

nets:
  N1: C1.-, FET1.source
  N2: C1.+, D1.cathode, MOTOR1.POS
  N3: D1.anode, FET1.drain, MOTOR1.NEG
  N4: FET1.gate, R1.Pin_1
  N5: C3.-, FET2.source
  N6: C3.+, D2.cathode, MOTOR2.POS
  N7: D2.anode, FET2.drain, MOTOR2.NEG
  N8: FET2.gate, R2.Pin_1
  N9: R3.Pin_1, FET3.gate
  N10: D3.cathode, C4.+
  N11: D3.anode, FET3.drain, MOTOR3.NEG
  N12: FET3.source, C4.-
  N13: C5.-, FET4.source
  N14: C5.+, D4.cathode
  N15: D4.anode, FET4.drain, MOTOR4.NEG
  N16: FET4.gate, R4.Pin_1

custom parts:
  STP16NF06 N-Channel Power MOSFET: STP16NF06 N-channel Power MOSFET
  Vibration Motor: An eccentric vibration motor!
