# Fritzing sketch bread-and-perma-combo (saved by Fritzing 0.9.0b)
breadboards: 1

parts:
  proto2 = Adafruit_PermaProto_1_4_Board  # not connected
  C10 = Electrolytic Capacitor [capacitance=10μF package="0605 [SMD, electrolytic]"]  # not connected
  D10 = Schottky Diode [part_number=1N5817 package="300 mil [THT]"]
  FET10 = STP16NF06 N-Channel Power MOSFET
  R9 = Resistor [tolerance=±5% resistance=220 package="1206 [SMD]"]

nets:
  N1: D10.anode, FET10.drain
  N2: FET10.gate, R9.Pin_1

custom parts:
  STP16NF06 N-Channel Power MOSFET: STP16NF06 N-channel Power MOSFET
