# Fritzing sketch bread-and-perma-combo2 (saved by Fritzing 0.9.0b)
breadboards: 1

parts:
  proto2 = Adafruit_PermaProto_1_4_Board
  PART1 = Motor Driver 1A Dual TB6612FNG [part_number=ROB_09457]  # not connected
  PART2 = Motor Driver 1A Dual TB6612FNG [part_number=ROB_09457]
  MOTOR1 = Vibration Motor
  MOTOR2 = Vibration Motor
  Part1 = Arduino Uno (Rev3)
  Part2 = Adafruit LSM9DS1 9DoF Breakout [part_number="Adafruit #3387"]

nets:
  N1: proto2.connectorA1, Part1.A0
  N2: proto2.connectorA2, proto2.connectorX2
  N3: proto2.connectorA3, proto2.connectorW3
  N4: proto2.connectorA4, proto2.connectorX4
  N5: proto2.connectorA5, proto2.connectorX5
  N6: proto2.connectorA6, proto2.connectorW6
  N7: proto2.connectorA7, Part1.A1
  N8: proto2.connectorA8, proto2.connectorX8
  N9: proto2.connectorA12, proto2.connectorW12
  N10: proto2.connectorA13, proto2.connectorX13
  N11: proto2.connectorA14, Part1.A4/SDA
  N12: proto2.connectorA15, Part1.A5/SCL
  N13: proto2.connectorE12, Part2.VDD
  N14: proto2.connectorE13, Part2.GND
  N15: proto2.connectorE14, Part2.SCL
  N16: proto2.connectorE15, Part2.SDA
  N17: proto2.connectorJ1, Part1.VIN
  N18: proto2.connectorJ8, proto2.connectorZ8
  N19: proto2.connectorY2, PART2.AIN2
  N20: proto2.connectorZ3, PART2.AIN1
  N21: PART2.STBY, MOTOR2.POS
  N22: PART2.BIN1, MOTOR2.NEG
  N23: PART2.BIN2, MOTOR1.POS
  N24: PART2.PWMB, MOTOR1.NEG

custom parts:
  Motor Driver 1A Dual TB6612FNG: The TB6612FNG motor driver can control up to two DC motors at a constant current of 1.2A (3.2A peak). Two input signals (IN1 and IN2) can be used to control the motor in one of four function modes - CW, CCW, short-brake, and stop. The two motor outputs (A and B) can be separately controlled, the speed of each motor is controlled via a PWM input signal with a frequency up to 100kHz. The STBY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
  Vibration Motor: An eccentric vibration motor!
  Adafruit LSM9DS1 9DoF Breakout: Add motion, direction and orientation sensing to your Arduino project with this all-in-one 9-DOF sensor. Inside the chip are three sensors, one is a classic 3-axis accelerometer, which can tell you which direction is down towards the Earth (by measuring gravity) or how fast the board is accelerating in 3D space. The other is a 3-axis magnetometer that can sense where the strongest magnetic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
